# Fritzing sketch Schematic (saved by Fritzing 0.9.3b)
breadboards: 1

parts:
  U1 = lolin
  R2 = Resistor [tolerance=±5% resistance=220 package=THT]
  R3 = Resistor [tolerance=±5% resistance=220 package=THT]
  LED2 = smd LED [color="Green (555nm)" package="0603 [SMD]"]
  LED1 = smd LED [color="Blue (430nm)" package="0603 [SMD]"]
  Part1 = MQ-7 breakout
  Part2 = MQ-7 breakout
  Part3 = KY-015 Temperature & Humidity Sensor Module [package="Breakout board"]

nets:
  N1: U1.connector5, Part2.AO
  N2: U1.connector6, Part1.AO
  VCC: U1.connector14, Part1.VCC, Part2.VCC, Part3.Vin
  GND: U1.connector15, Part1.GND, Part2.GND, Part3.-
  N3: U1.connector20, LED2.cathode, LED1.cathode
  N4: U1.connector22, Part3.S
  N5: U1.connector26, R3.Pin_0
  N6: U1.connector27, R2.Pin_0
  N7: R2.Pin_1, LED1.anode
  N8: R3.Pin_1, LED2.anode

notes:
  GND
  5.0V
  PIN5 STATUS LED
  PIN18 WIFI STATUS LED
  DHT11
  Temperature e Humidity
  MQ135
  MQ4

custom parts:
  MQ-7 breakout: SKU: 101282
  KY-015 Temperature & Humidity Sensor Module: KY-015 temperature and humidity sensor module, provides a low-latency serial interface to measure humidity and temperature.
